# Fritzing sketch scheme-test (saved by Fritzing 0.9.3b)
breadboards: 1

parts:
  U1 = MLX90614 [package=to-39]
  Raspberry_Pi_1 = Raspberry Pi 3 [part_number=RPI-3-V1.2]
  R1 = Resistor [tolerance=±5% resistance=220 package=THT]
  R2 = Resistor [tolerance=±5% resistance=220 package=THT]
  LED1 = smd LED [color="Red (633nm)" package="1206 [SMD]"]
  LED2 = smd LED [color="Red (633nm)" package="1206 [SMD]"]

nets:
  N1: U1.SCL_VZ, Raspberry_Pi_1.GPIO3
  N2: U1.PWM_SDA, Raspberry_Pi_1.GPIO2
  VDD: U1.VDD, Raspberry_Pi_1.5V
  N3: Raspberry_Pi_1.GPIO17, LED1.anode
  N4: Raspberry_Pi_1.GPIO27, LED2.anode
  N5: Raspberry_Pi_1.GND, R1.Pin_0, R2.Pin_0
  N6: R1.Pin_1, LED1.cathode
  N7: R2.Pin_1, LED2.cathode
